# Fritzing sketch ESP32S+Pulse+Neopixel-LED (saved by Fritzing 0.9.3b)
breadboards: 1

parts:
  U1 = ESP32S-HiLetgo [part_number=ESP32S-HiLetgo]
  Neopixel = Neopixel LED
  SEN3 = Pulse Sensor [package=SIP-3]

nets:
  N1: U1.GPIO36, SEN3.Signal
  GND: U1.GND, Neopixel.Ground, SEN3.GND
  VIN: U1.VIN, Neopixel.+5V, SEN3.VCC
  N2: U1.GPIO5, Neopixel.Data_In

notes:
  LED Flat side is on left
  - + data

custom parts:
  ESP32S-HiLetgo: HiLetgo ESP-WROOM-32 ESP32 ESP-32S Development Board 2.4GHz Dual-Mode WiFi + Bluetooth Dual Cores Microcontroller The ESP32 integrated with Antenna switches, RF Balun, power amplifiers, low-noise amplifiers, filters, and management modules, and the entire solution occupies the least area of PCB. 2.4 GHz Wi-Fi plus Bluetooth dual-mode chip, with TSMC Ultra-low power consumption 40nm technology,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
  Neopixel LED: Neopixel LED 8mm (left side is flat)
  Pulse Sensor: Pulse Sensor Optical Heart Beat Sensor
